// Logisim project 8_bit_Computer.circ as structural Verilog: 5 circuits, main circuit main
module main (
  input  WE4,
  input  OE4,
  input  WE,
  input  OE,
  input  WE3,
  input  OE3,
  input  WE2,
  input  [7:0] ForTesting,
  output [7:0] IRContent,
  output WE5,
  output OE5,
  output [7:0] RegisterAcontent,
  output [7:0] ALUResult,
  output [7:0] out_14,
  output [7:0] RegisterBcontent
);

  wire clock_1_out;
  wire [2:0] undriven;
  wire [3:0] bitselector_1_out, mar_1_dout;
  wire [7:0] alu_1_aluresult, InstructionRegister_dout, OutuputRegister_sd;

  Clock clock_1 (.out(clock_1_out));
  Registercell InstructionRegister (
    .WE(WE4), .Clock(clock_1_out), .OE(OE4), .Din(ForTesting), .Dout(InstructionRegister_dout), .SD(IRContent));
  Registercell RegisterA (.WE(WE), .Clock(clock_1_out), .Din(ForTesting), .SD(RegisterAcontent));  // open: OE, Dout
  ALU alu_1 (
    .RegA(RegisterAcontent), .RegB(RegisterBcontent), .OE(OE), .Dout(ForTesting), .ALUResult(alu_1_aluresult));  // open: CarryOut
  Registercell RegisterB (.WE(WE2), .Clock(clock_1_out), .Din(ForTesting), .SD(RegisterBcontent));  // open: OE, Dout
  LED D7 (.in(ForTesting[7]));
  LED D6 (.in(ForTesting[6]));
  LED D5 (.in(ForTesting[5]));
  BitSelector bitselector_1 (.in(InstructionRegister_dout), .out(bitselector_1_out[0]), .sel(undriven));
  LED D4 (.in(ForTesting[4]));
  LED D3 (.in(ForTesting[3]));
  LED D2 (.in(ForTesting[2]));
  LED D1 (.in(ForTesting[1]));
  LED D0 (.in(ForTesting[0]));
  MAR mar_1 (.WE(WE5), .Clock(clock_1_out), .OE(OE5), .Din(bitselector_1_out), .Dout(mar_1_dout));  // open: SD
  Registercell OutuputRegister (
    .WE(WE3), .Clock(clock_1_out), .OE(OE3),
    .Din({ForTesting[0], ForTesting[1], ForTesting[2], ForTesting[3], ForTesting[4], ForTesting[5], ForTesting[6], ForTesting[7]}),
    .Dout(ForTesting), .SD(OutuputRegister_sd));
  Registercell registercell_1 (
    .WE(WE5), .Clock(clock_1_out), .OE(OE5), .Din(ForTesting), .Dout(ForTesting));  // open: SD
  LED led_1 (.in(ForTesting[7]));
  LED led_2 (.in(ForTesting[6]));
  LED led_3 (.in(ForTesting[5]));
  LED led_4 (.in(ForTesting[4]));
  LED led_5 (.in(ForTesting[3]));
  LED led_6 (.in(ForTesting[2]));
  LED led_7 (.in(ForTesting[1]));
  LED led_8 (.in(ForTesting[0]));

  // Notes on the sheet:
  //   Internal Data Bus
  //   0
  //   External Adress Bus
endmodule

module Memory (
  input  WE,
  input  Clock,
  input  Din,
  input  OE,
  input  Reset,
  output Dout,
  output SD
);

  wire and_1_out, and_2_out, not_1_out, or_1_out;

  not not_1 (not_1_out, WE);
  and and_1 (and_1_out, SD, not_1_out);
  and and_2 (and_2_out, WE, Din);
  or or_1 (or_1_out, and_1_out, and_2_out);
  D_Flip_Flop d_ff_1 (.D(or_1_out), .clk(Clock), .Q(SD), .reset(Reset));  // open: Qn, preset
  assign Dout = OE ? SD : 1'bz;  // Controlled_Buffer controlled_buffer_1
endmodule

module Registercell (
  input  WE,
  input  Clock,
  input  OE,
  input  [7:0] Din,
  output [7:0] Dout,
  output [7:0] SD
);

  Memory memory_1 (.WE(WE), .Clock(Clock), .Din(Din[0]), .OE(OE), .Dout(Dout[0]), .SD(SD[0]));  // open: Reset
  Memory memory_2 (.WE(WE), .Clock(Clock), .Din(Din[1]), .OE(OE), .Dout(Dout[1]), .SD(SD[1]));  // open: Reset
  Memory memory_3 (.WE(WE), .Clock(Clock), .Din(Din[2]), .OE(OE), .Dout(Dout[2]), .SD(SD[2]));  // open: Reset
  Memory memory_4 (.WE(WE), .Clock(Clock), .Din(Din[3]), .OE(OE), .Dout(Dout[3]), .SD(SD[3]));  // open: Reset
  Memory memory_5 (.WE(WE), .Clock(Clock), .Din(Din[4]), .OE(OE), .Dout(Dout[4]), .SD(SD[4]));  // open: Reset
  Memory memory_6 (.WE(WE), .Clock(Clock), .Din(Din[5]), .OE(OE), .Dout(Dout[5]), .SD(SD[5]));  // open: Reset
  Memory memory_7 (.WE(WE), .Clock(Clock), .Din(Din[6]), .OE(OE), .Dout(Dout[6]), .SD(SD[6]));  // open: Reset
  Memory memory_8 (.WE(WE), .Clock(Clock), .Din(Din[7]), .OE(OE), .Dout(Dout[7]), .SD(SD[7]));  // open: Reset
endmodule

module MAR (
  input  WE,
  input  Clock,
  input  OE,
  input  [3:0] Din,
  output [3:0] Dout,
  output [3:0] SD
);

  Memory memory_1 (.WE(WE), .Clock(Clock), .Din(Din[0]), .OE(OE), .Dout(Dout[0]), .SD(SD[0]));  // open: Reset
  Memory memory_2 (.WE(WE), .Clock(Clock), .Din(Din[1]), .OE(OE), .Dout(Dout[1]), .SD(SD[1]));  // open: Reset
  Memory memory_3 (.WE(WE), .Clock(Clock), .Din(Din[2]), .OE(OE), .Dout(Dout[2]), .SD(SD[2]));  // open: Reset
  Memory memory_4 (.WE(WE), .Clock(Clock), .Din(Din[3]), .OE(OE), .Dout(Dout[3]), .SD(SD[3]));  // open: Reset
endmodule

module ALU (
  input  [7:0] RegA,
  input  [7:0] RegB,
  input  OE,
  output [7:0] Dout,
  output [7:0] ALUResult,
  output CarryOut
);

  Adder adder_1 (.a(RegA), .b(RegB), .out(ALUResult), .cout(CarryOut));  // open: cin
  assign Dout = OE ? ALUResult : 8'bz;  // Controlled_Buffer controlled_buffer_1
endmodule
